# Fritzing sketch fingercode (saved by Fritzing 0.6.3b)
stripboards: 1

parts:
  IC1 = IC, DIP package, 24 pins [chip_label=IC spacing=300mil]
  J1 = female pin header, 4 pins [form="♀ (female)"]
  IC2 = IC, DIP package, 24 pins [chip_label=IC spacing=300mil]
  IC3 = IC, DIP package, 24 pins [chip_label=IC spacing=300mil]
  IC4 = IC, DIP package, 24 pins [chip_label=IC spacing=300mil]
  IC5 = IC, DIP package, 24 pins [chip_label=IC spacing=300mil]
  IC6 = IC, DIP package, 24 pins [chip_label=IC spacing=300mil]
  IC7 = IC, DIP package, 24 pins [chip_label=IC spacing=300mil]
  IC8 = IC, DIP package, 24 pins [chip_label=IC spacing=300mil]
  J2 = female pin header, 8 pins [form="♀ (female)"]
  J3 = female pin header, 8 pins [form="♀ (female)"]

nets:
  N1: IC1.pin8, J2.pin1
  N2: IC1.pin9, J3.pin1
  N3: IC1.pin10, J1.pin1, IC2.pin10, IC3.pin10, IC4.pin10, IC5.pin10, IC6.pin10, IC7.pin10, IC8.pin10
  N4: IC1.pin11, J1.pin2, IC2.pin11, IC3.pin11, IC4.pin11, IC5.pin11, IC6.pin11, IC7.pin11, IC8.pin11
  N5: IC1.pin13, J1.pin4, IC2.pin13, IC3.pin13, IC4.pin13, IC5.pin13, IC6.pin13, IC7.pin13, IC8.pin13
  N6: IC1.pin14, J1.pin3, IC2.pin14, IC3.pin14, IC4.pin14, IC5.pin14, IC6.pin14, IC7.pin14, IC8.pin14
  N7: IC2.pin8, J2.pin2
  N8: IC2.pin9, J3.pin2
  N9: IC3.pin8, J2.pin3
  N10: IC3.pin9, J3.pin3
  N11: IC4.pin8, J2.pin4
  N12: IC4.pin9, J3.pin4
  N13: IC5.pin8, J2.pin5
  N14: IC5.pin9, J3.pin5
  N15: IC6.pin8, J2.pin6
  N16: IC6.pin9, J3.pin6
  N17: IC7.pin8, J2.pin7
  N18: IC7.pin9, J3.pin7
  N19: IC8.pin8, J2.pin8
  N20: IC8.pin9, J3.pin8
